# Fritzing sketch boat-final (saved by Fritzing 0.9.1b)
breadboards: 1

parts:
  Q1 = Basic FET N-Channel [package="TO220 [THT]"]
  M1 = DC Motor
  D1 = Rectifier Diode [part_number=1N4001 package="300 mil [THT]"]
  Part1 = Spark Core (v1.0)
  R1 = Resistor [tolerance=±5% resistance=330 package=THT]
  VCC1 = 4 x AAA Battery Mount

nets:
  N1: Q1.gate, R1.Pin_0
  N2: Q1.drain, M1.pin_2, D1.cathode
  N3: Q1.source, D1.anode, Part1.GND, VCC1.-
  N4: M1.pin_1, Part1.VIN, VCC1.+
  N5: Part1.D0, R1.Pin_1
