# Fritzing sketch bot-start (saved by Fritzing 0.9.1b)
breadboards: 1

parts:
  Part1 = Spark Core (v1.0)
  J1 = Basic Servo

nets:
  GND: Part1.GND, J1.gnd
  VIN: Part1.VIN, J1.vcc
  N1: Part1.D0, J1.pulse

notes:
  Yellow wire is actually white
  on our servos
