# Fritzing sketch bot-two-motors (saved by Fritzing 0.9.1b)
breadboards: 1

parts:
  Part1 = Spark Core (v1.0)
  J1 = Basic Servo
  J2 = Basic Servo
  VCC1 = 4 x AAA Battery Mount

nets:
  GND: Part1.GND, J1.gnd, J2.gnd
  VCC: Part1.VIN, J1.vcc, J2.vcc, VCC1.+
  N1: Part1.D0, J1.pulse
  N2: Part1.D1, J2.pulse

notes:
  Yellow wire is actually white
  on our servos
